// Logisim project ALU.circ as structural Verilog: 11 circuits, main circuit main
module main (
  input  E,
  input  A0,
  input  A1,
  input  A2,
  input  B0,
  input  B1,
  input  B2,
  input  C0,
  input  C1,
  output R0,
  output R1,
  output R2,
  output CyBwo,
  output Ov,
  output Z
);

  ALU alu_1 (
    .E(E), .A0(A0), .A1(A1), .A2(A2), .B1(B1), .B2(B2), .C0(C0), .C1(C1), .R0(R0), .R1(R1), .R2(R2),
    .CyBwo(CyBwo), .Ov(Ov), .B0(B0), .Z(Z));
endmodule

module ALU (
  input  C0,
  input  C1,
  input  E,
  input  A0,
  input  A1,
  input  A2,
  input  B0,
  input  B1,
  input  B2,
  output R0,
  output R1,
  output R2,
  output Ov,
  output Z,
  output CyBwo
);

  wire Bw, Cy, flags_1_cybwo, flags_1_ov, flags_1_z, mux_4x1_1_c0_2, mux_4x1_1_c1_2, mux_4x1_1_s,
       mux_4x1_2_c0_2, mux_4x1_2_c1_2, mux_4x1_2_s, mux_4x1_3_c0_2, mux_4x1_3_s, NAND0, NAND1, NAND2, NOR0,
       NOR1, NOR2, SUB0, SUB1, SUB2, SUM0, SUM1, SUM2;

  Somador somador_1 (.A0(A0), .B0(B0), .A1(A1), .B1(B1), .A2(A2), .B2(B2), .S0(SUM0), .S1(SUM1), .S2(SUM2), .CyOut(Cy));
  Subtrator subtrator_1 (
    .A0(A0), .B0(B0), .A1(A1), .B1(B1), .A2(A2), .B2(B2), .S0(SUB0), .S1(SUB1), .S2(SUB2), .BwOut(Bw));
  NOR nor_1 (.A0(A0), .B0(B0), .A1(A1), .B1(B1), .A2(A2), .B2(B2), .S0(NOR0), .S1(NOR1), .S2(NOR2));
  NAND nand_1 (.A0(A0), .B0(B0), .A1(A1), .B1(B1), .A2(A2), .B2(B2), .S0(NAND0), .S1(NAND1), .S2(NAND2));
  MUX_4X1 mux_4x1_1 (
    .A(SUM0), .B(SUB0), .C(NOR0), .D(NAND0), .C0(C0), .C1(C1), .S(mux_4x1_1_s), .C0_2(mux_4x1_1_c0_2),
    .C1_2(mux_4x1_1_c1_2));
  MUX_4X1 mux_4x1_2 (
    .A(SUM1), .B(SUB1), .C(NOR1), .D(NAND1), .C0(mux_4x1_1_c0_2), .C1(mux_4x1_1_c1_2), .S(mux_4x1_2_s),
    .C0_2(mux_4x1_2_c0_2), .C1_2(mux_4x1_2_c1_2));
  MUX_4X1 mux_4x1_3 (
    .A(SUM2), .B(SUB2), .C(NOR2), .D(NAND2), .C0(mux_4x1_2_c0_2), .C1(mux_4x1_2_c1_2), .S(mux_4x1_3_s),
    .C0_2(mux_4x1_3_c0_2));  // open: C1_2
  and and_1 (R0, E, mux_4x1_1_s);
  and and_2 (R1, E, mux_4x1_2_s);
  and and_3 (R2, E, mux_4x1_3_s);
  Flags flags_1 (
    .A2(A2), .B2(B2), .R0(mux_4x1_1_s), .R1(mux_4x1_2_s), .R2(mux_4x1_3_s), .Carry(Cy), .Borrow(Bw),
    .C0(mux_4x1_3_c0_2), .OV(flags_1_ov), .Z(flags_1_z), .CyBwo(flags_1_cybwo));
  and and_4 (Ov, E, flags_1_ov);
  and and_5 (Z, E, flags_1_z);
  and and_6 (CyBwo, E, flags_1_cybwo);
endmodule

module Somador (
  input  A0,
  input  B0,
  input  A1,
  input  B1,
  input  A2,
  input  B2,
  output S0,
  output S1,
  output S2,
  output CyOut
);

  wire somador_1_bit_1_cyout, somador_1_bit_2_cyout;

  Somador_1_Bit somador_1_bit_1 (.CyIn(1'b0), .A(A0), .B(B0), .S(S0), .CyOut(somador_1_bit_1_cyout));
  Somador_1_Bit somador_1_bit_2 (.CyIn(somador_1_bit_1_cyout), .A(A1), .B(B1), .S(S1), .CyOut(somador_1_bit_2_cyout));
  Somador_1_Bit somador_1_bit_3 (.CyIn(somador_1_bit_2_cyout), .A(A2), .B(B2), .S(S2), .CyOut(CyOut));
endmodule

module Subtrator (
  input  A0,
  input  B0,
  input  A1,
  input  B1,
  input  A2,
  input  B2,
  output S0,
  output S1,
  output S2,
  output BwOut
);

  wire subtrator_1_bit_1_bwout, subtrator_1_bit_2_bwout;

  Subtrator_1_Bit subtrator_1_bit_1 (.BwIn(1'b0), .A(A0), .B(B0), .S(S0), .BwOut(subtrator_1_bit_1_bwout));
  Subtrator_1_Bit subtrator_1_bit_2 (
    .BwIn(subtrator_1_bit_1_bwout), .A(A1), .B(B1), .S(S1), .BwOut(subtrator_1_bit_2_bwout));
  Subtrator_1_Bit subtrator_1_bit_3 (.BwIn(subtrator_1_bit_2_bwout), .A(A2), .B(B2), .S(S2), .BwOut(BwOut));
endmodule

module NAND (
  input  A0,
  input  B0,
  input  A1,
  input  B1,
  input  A2,
  input  B2,
  output S0,
  output S1,
  output S2
);

  nand nand_1 (S0, A0, B0);
  nand nand_2 (S1, A1, B1);
  nand nand_3 (S2, A2, B2);
endmodule

module NOR (
  input  A0,
  input  B0,
  input  A1,
  input  B1,
  input  A2,
  input  B2,
  output S0,
  output S1,
  output S2
);

  nor nor_1 (S0, A0, B0);
  nor nor_2 (S1, A1, B1);
  nor nor_3 (S2, A2, B2);
endmodule

module Somador_1_Bit (
  input  CyIn,
  input  A,
  input  B,
  output S,
  output CyOut
);

  wire and_1_out, and_2_out, and_3_out;

  and and_1 (and_1_out, A, B);
  and and_2 (and_2_out, A, CyIn);
  and and_3 (and_3_out, CyIn, B);
  xor xor_1 (S, CyIn, A, B);
  or or_1 (CyOut, and_1_out, and_2_out, and_3_out);
endmodule

module Subtrator_1_Bit (
  input  BwIn,
  input  A,
  input  B,
  output S,
  output BwOut
);

  wire and_1_out, and_2_out, and_3_out;

  and and_1 (and_1_out, ~A, B);  // AND_Gate
  and and_2 (and_2_out, ~A, BwIn);  // AND_Gate
  and and_3 (and_3_out, B, BwIn);
  xor xor_1 (S, BwIn, A, B);
  or or_1 (BwOut, and_1_out, and_2_out, and_3_out);
endmodule

module MUX_4X1 (
  input  A,
  input  B,
  input  C,
  input  D,
  input  C0,
  input  C1,
  output S,
  output C0_2,
  output C1_2
);

  wire and_1_out, and_2_out, and_3_out, and_4_out;

  and and_1 (and_1_out, A, ~C0, ~C1);  // AND_Gate
  and and_2 (and_2_out, B, C0, ~C1);  // AND_Gate
  and and_3 (and_3_out, C, ~C0, C1);  // AND_Gate
  and and_4 (and_4_out, D, C0, C1);
  or or_1 (S, and_1_out, and_2_out, and_3_out, and_4_out);

  assign C0_2 = C0;
  assign C1_2 = C1;
endmodule

module Flags (
  input  A2,
  input  B2,
  input  R0,
  input  R1,
  input  R2,
  input  Carry,
  input  Borrow,
  input  C0,
  output OV,
  output Z,
  output CyBwo
);

  wire and_1_out, and_2_out;

  and and_1 (and_1_out, ~A2, ~B2, R2);  // AND_Gate
  and and_2 (and_2_out, A2, B2, ~R2);  // AND_Gate
  and and_3 (Z, ~R0, ~R1, ~R2);  // AND_Gate
  MUX_2X1 mux_2x1_1 (.A(Carry), .B(Borrow), .C(C0), .S(CyBwo));
  or or_1 (OV, and_1_out, and_2_out);
endmodule

module MUX_2X1 (
  input  A,
  input  B,
  input  C,
  output S
);

  wire and_1_out, and_2_out;

  and and_1 (and_1_out, A, ~C);  // AND_Gate
  and and_2 (and_2_out, B, C);
  or or_1 (S, and_1_out, and_2_out);
endmodule
