// Logisim project Tings.circ as structural Verilog
module Somador_1_Bit (
  input  A,
  input  B,
  input  CyIn,
  output S,
  output CyOut
);

  wire and_1_out, and_2_out, and_3_out;

  xor xor_1 (S, A, B, CyIn);
  and and_1 (and_1_out, A, B);
  and and_2 (and_2_out, A, CyIn);
  and and_3 (and_3_out, B, CyIn);
  or or_1 (CyOut, and_1_out, and_2_out, and_3_out);
endmodule

module Subtrator_1_Bit (
  input  A,
  input  B,
  input  BwIn,
  output S,
  output BwOut
);

  wire and_1_out, and_2_out, and_3_out, not_1_out, not_2_out;

  not not_1 (not_1_out, A);
  not not_2 (not_2_out, A);
  xor xor_1 (S, A, B, BwIn);
  and and_1 (and_1_out, not_1_out, B);
  and and_2 (and_2_out, not_2_out, BwIn);
  and and_3 (and_3_out, B, BwIn);
  or or_1 (BwOut, and_1_out, and_2_out, and_3_out);
endmodule

module NAND (
  input  A,
  input  B,
  output S
);

  wire and_1_out;

  and and_1 (and_1_out, A, B);
  not not_1 (S, and_1_out);
endmodule

module NOR (
  input  A,
  input  B,
  output S
);

  wire or_1_out;

  or or_1 (or_1_out, A, B);
  not not_1 (S, or_1_out);
endmodule

module Z (
  input  A0,
  input  A1,
  input  A2,
  output Z
);

  wire not_1_out, not_2_out, not_3_out;

  not not_1 (not_1_out, A0);
  not not_2 (not_2_out, A1);
  not not_3 (not_3_out, A2);
  and and_1 (Z, not_1_out, not_2_out, not_3_out);
endmodule

module OV (
  input  A2,
  input  B2,
  input  R2,
  output OV
);

  wire and_1_out, and_2_out, not_1_out, not_2_out, not_3_out;

  not not_1 (not_1_out, A2);
  not not_2 (not_2_out, B2);
  not not_3 (not_3_out, R2);
  and and_1 (and_1_out, not_1_out, not_2_out, R2);
  and and_2 (and_2_out, A2, B2, not_3_out);
  or or_1 (OV, and_1_out, and_2_out);
endmodule
